# Fritzing sketch led-rgb-fader (saved by Fritzing 0.7.10b)
breadboards: 1

parts:
  Arduino = Arduino
  R1 = Resistor [tolerance=±5% resistance=220 package=THT]
  R2 = Resistor [tolerance=±5% resistance=220 package=THT]
  R3 = Resistor [tolerance=±5% resistance=220 package=THT]
  R4 = Rotary Potentiometer (Small) [maximum_resistance=100kΩ]
  LED = RGB LED - (4 legs) [package="5 mm [THT]"]

nets:
  N1: Arduino.D11, R1.Pin_1
  N2: Arduino.D10, R2.Pin_1
  N3: Arduino.D9, R3.Pin_1
  N4: Arduino.+5V, R4.leg2, LED.common_anode
  N5: Arduino.GND, R4.leg1
  N6: Arduino.A0, R4.wiper
  N7: R1.Pin_0, LED.red_cathode
  N8: R2.Pin_0, LED.green_cathode
  N9: R3.Pin_0, LED.blue_cathode
