# Fritzing sketch pushbutton-led (saved by Fritzing 0.7.10b)
breadboards: 1

parts:
  Arduino1 = Arduino
  S1 = Pushbutton [package="[THT]"]
  LED1 = LED - 5mm [color="Red (633nm)" package="5 mm [THT]"]
  R1 = Resistor [tolerance=±5% resistance=10k package=THT]
  R2 = Resistor [tolerance=±5% resistance=220 package=THT]  # not connected

nets (from the schematic view):
  N1: Arduino1.GND, LED1.cathode, R1.Pin_1
  N2: Arduino1.D13, S1.Pin_1, S1.Pin_2, R1.Pin_0
  N3: Arduino1.D10, Arduino1.D8
  N4: Arduino1.D2, LED1.anode
  N5: Arduino1.+5V, S1.Pin_3, S1.Pin_4
