# Fritzing sketch pushbutton-led (saved by Fritzing 0.7.10b)
breadboards: 1

parts:
  Arduino1 = Arduino
  S1 = Pushbutton [package="[THT]"]
  LED1 = LED - 5mm [color="Red (633nm)" package="5 mm [THT]"]
  R1 = Resistor [tolerance=±5% resistance=10k package=THT]
  R2 = Resistor [tolerance=±5% resistance=220 package=THT]

nets:
  N1: Arduino1.GND, LED1.cathode, R1.Pin_1
  N2: Arduino1.D13, S1.Pin_1, S1.Pin_2, R1.Pin_0
  N3: Arduino1.D2, R2.Pin_1
  N4: Arduino1.+5V, S1.Pin_3, S1.Pin_4
  N5: LED1.anode, R2.Pin_0
